# Fritzing sketch PAECE_LAB1_POT (saved by Fritzing 0.9.3b)
breadboards: 1

parts:
  U1 = POT [package=pot_alpha_rv16af-20]
  Part1 = Arduino Uno (Rev3) - ICSP

nets:
  N1: U1.A, Part1.5V
  N2: U1.S, Part1.A0
  N3: U1.E, Part1.GND
